# Fritzing sketch cablage-base (saved by Fritzing 0.9.3b)

parts:
  Part1 = Arduino Uno (Rev3) - ICSP
  Part2 = NRF24L01

nets:
  N1: Part1.D8, Part2.CSN
  N2: Part1.D11_PWM/MOSI, Part2.MOSI
  N3: Part1.D12/MISO, Part2.MISO
  N4: Part1.D13/SCK, Part2.SCK
  N5: Part1.D7, Part2.CE
  3V3: Part1.3V3, Part2.VCC
  GND: Part1.GND, Part2.GND
