# Fritzing sketch cablage-emetteur (saved by Fritzing 0.9.3b)

parts:
  Part1 = Arduino Pro Mini v13
  Part2 = NRF24L01
  U1 = LIPO-1000mAh [package=lipo-1000]

nets:
  GND: Part1.GND, Part2.GND, U1.-
  VCC: Part1.VCC, Part2.VCC, U1.+
  N1: Part1.D13/SCK, Part2.SCK
  N2: Part1.D12/MISO, Part2.MISO
  N3: Part1.D11_PWM/MOSI, Part2.MOSI
  N4: Part1.D8, Part2.CSN
  N5: Part1.D7, Part2.CE
